# Fritzing sketch midi_drums (saved by Fritzing 1.0.4)

parts:
  Arduino_Leonardo = Arduino Leonardo (Rev3b)
  J1 = Piezo Speaker
  J2 = Piezo Speaker
  J3 = Piezo Speaker
  J4 = Piezo Speaker
  J5 = Piezo Speaker
  J6 = Piezo Speaker
  J7 = Piezo Speaker
  R1 = Resistor [tolerance=±5% resistance=1M package="0805 [SMD]"]
  R2 = Resistor [tolerance=±5% resistance=1M package="0805 [SMD]"]
  R3 = Resistor [tolerance=±5% resistance=1M package="0805 [SMD]"]
  R4 = Resistor [tolerance=±5% resistance=1M package="0805 [SMD]"]
  R5 = Resistor [tolerance=±5% resistance=1M package="0805 [SMD]"]
  R6 = Resistor [tolerance=±5% resistance=1M package="0805 [SMD]"]
  R7 = Resistor [tolerance=±5% resistance=1M package="0805 [SMD]"]
  Bass_Pedal = SPST Switch [package=switch-spdt-smd]

nets:
  N1: Arduino_Leonardo.D4/A6, J7.pin1, R7.Pin_1
  N2: Arduino_Leonardo.5V, J1.pin2, J2.pin2, J3.pin2, J4.pin2, J5.pin2, J6.pin2, J7.pin2
  N3: Arduino_Leonardo.GND, R1.Pin_0, R2.Pin_0, R3.Pin_0, R4.Pin_0, R5.Pin_0, R6.Pin_0, R7.Pin_0, Bass_Pedal.S
  N4: Arduino_Leonardo.A0, J1.pin1, R1.Pin_1
  N5: Arduino_Leonardo.A1, J2.pin1, R2.Pin_1
  N6: Arduino_Leonardo.A2, J3.pin1, R3.Pin_1
  N7: Arduino_Leonardo.A3, J4.pin1, R4.Pin_1
  N8: Arduino_Leonardo.A4, J5.pin1, R5.Pin_1
  N9: Arduino_Leonardo.A5, J6.pin1, R6.Pin_1
  N10: Arduino_Leonardo.SCL, Bass_Pedal.P
